// Logisim project ULA.circ as structural Verilog: 5 circuits, main circuit main
module main (
  input  [31:0] Entrada_A,
  input  [31:0] Entrada_B,
  input  [4:0] Seletor,
  output out_4,
  output [31:0] \Saída_S 
);

  wire celula_2_cout, celula_2_s, celula_3_cout, celula_4_cout, celula_5_cout, celula_6_cout, celula_7_cout,
       celula_8_cout, celula_9_cout, celula_10_cout, celula_11_cout, celula_12_cout, celula_13_cout,
       celula_14_cout, celula_15_cout, celula_16_cout, celula_17_cout, celula_18_cout, celula_19_cout,
       celula_20_cout, celula_21_cout, celula_22_cout, celula_23_cout, celula_24_cout, celula_25_cout,
       celula_26_cout, celula_27_cout, celula_28_cout, celula_29_cout, celula_30_cout, celula_31_cout,
       celula_32_cout, overflowcontroler_1_overflow;

  Celula celula_1 (
    .Cin(celula_2_cout), .b(Entrada_B[30]), .a(Entrada_A[30]), .Seletor(Seletor), .S(Entrada_A[31]),
    .Cout(Entrada_A[31]));
  Celula celula_2 (
    .Cin(celula_4_cout), .b(Entrada_B[31]), .a(Entrada_A[31]), .Seletor(Seletor), .S(celula_2_s),
    .Cout(celula_2_cout));
  Celula celula_3 (
    .Cin(Entrada_A[31]), .b(Entrada_B[28]), .a(Entrada_A[28]), .Seletor(Seletor), .S(Entrada_A[29]),
    .Cout(celula_3_cout));
  Celula celula_4 (
    .Cin(celula_6_cout), .b(Entrada_B[29]), .a(Entrada_A[29]), .Seletor(Seletor), .S(Entrada_A[30]),
    .Cout(celula_4_cout));
  Celula celula_5 (
    .Cin(celula_3_cout), .b(Entrada_B[26]), .a(Entrada_A[26]), .Seletor(Seletor), .S(Entrada_A[27]),
    .Cout(celula_5_cout));
  Celula celula_6 (
    .Cin(celula_8_cout), .b(Entrada_B[27]), .a(Entrada_A[27]), .Seletor(Seletor), .S(Entrada_A[28]),
    .Cout(celula_6_cout));
  Celula celula_7 (
    .Cin(celula_5_cout), .b(Entrada_B[24]), .a(Entrada_A[24]), .Seletor(Seletor), .S(Entrada_A[25]),
    .Cout(celula_7_cout));
  Celula celula_8 (
    .Cin(celula_10_cout), .b(Entrada_B[25]), .a(Entrada_A[25]), .Seletor(Seletor), .S(Entrada_A[26]),
    .Cout(celula_8_cout));
  Celula celula_9 (
    .Cin(celula_7_cout), .b(Entrada_B[23]), .a(Entrada_A[22]), .Seletor(Seletor), .S(Entrada_A[23]),
    .Cout(celula_9_cout));
  Celula celula_10 (
    .Cin(celula_12_cout), .b(Entrada_B[22]), .a(Entrada_A[23]), .Seletor(Seletor), .S(Entrada_A[24]),
    .Cout(celula_10_cout));
  Celula celula_11 (
    .Cin(celula_9_cout), .b(Entrada_B[21]), .a(Entrada_A[20]), .Seletor(Seletor), .S(Entrada_A[21]),
    .Cout(celula_11_cout));
  Celula celula_12 (
    .Cin(celula_14_cout), .b(Entrada_B[20]), .a(Entrada_A[21]), .Seletor(Seletor), .S(Entrada_A[22]),
    .Cout(celula_12_cout));
  Celula celula_13 (
    .Cin(celula_11_cout), .b(Entrada_B[19]), .a(Entrada_A[18]), .Seletor(Seletor), .S(Entrada_A[19]),
    .Cout(celula_13_cout));
  Celula celula_14 (
    .Cin(celula_16_cout), .b(Entrada_B[18]), .a(Entrada_A[19]), .Seletor(Seletor), .S(Entrada_A[20]),
    .Cout(celula_14_cout));
  Celula celula_15 (
    .Cin(celula_13_cout), .b(Entrada_B[17]), .a(Entrada_A[16]), .Seletor(Seletor), .S(Entrada_A[17]),
    .Cout(celula_15_cout));
  Celula celula_16 (
    .Cin(celula_18_cout), .b(Entrada_B[16]), .a(Entrada_A[17]), .Seletor(Seletor), .S(Entrada_A[18]),
    .Cout(celula_16_cout));
  Celula celula_17 (
    .Cin(celula_15_cout), .b(Entrada_B[15]), .a(Entrada_A[14]), .Seletor(Seletor), .S(Entrada_A[15]),
    .Cout(celula_17_cout));
  Celula celula_18 (
    .Cin(celula_20_cout), .b(Entrada_B[14]), .a(Entrada_A[15]), .Seletor(Seletor), .S(Entrada_A[16]),
    .Cout(celula_18_cout));
  Celula celula_19 (
    .Cin(celula_17_cout), .b(Entrada_B[13]), .a(Entrada_A[12]), .Seletor(Seletor), .S(Entrada_A[13]),
    .Cout(celula_19_cout));
  Celula celula_20 (
    .Cin(celula_22_cout), .b(Entrada_B[12]), .a(Entrada_A[13]), .Seletor(Seletor), .S(Entrada_A[14]),
    .Cout(celula_20_cout));
  Celula celula_21 (
    .Cin(celula_19_cout), .b(Entrada_B[11]), .a(Entrada_A[10]), .Seletor(Seletor), .S(Entrada_A[11]),
    .Cout(celula_21_cout));
  Celula celula_22 (
    .Cin(celula_24_cout), .b(Entrada_B[10]), .a(Entrada_A[11]), .Seletor(Seletor), .S(Entrada_A[12]),
    .Cout(celula_22_cout));
  Celula celula_23 (
    .Cin(celula_21_cout), .b(Entrada_B[9]), .a(Entrada_A[8]), .Seletor(Seletor), .S(Entrada_A[9]),
    .Cout(celula_23_cout));
  Celula celula_24 (
    .Cin(celula_26_cout), .b(Entrada_B[8]), .a(Entrada_A[9]), .Seletor(Seletor), .S(Entrada_A[10]),
    .Cout(celula_24_cout));
  Celula celula_25 (
    .Cin(celula_23_cout), .b(Entrada_B[7]), .a(Entrada_A[6]), .Seletor(Seletor), .S(Entrada_A[7]),
    .Cout(celula_25_cout));
  Celula celula_26 (
    .Cin(celula_28_cout), .b(Entrada_B[6]), .a(Entrada_A[7]), .Seletor(Seletor), .S(Entrada_A[8]),
    .Cout(celula_26_cout));
  Celula celula_27 (
    .Cin(celula_25_cout), .b(Entrada_B[5]), .a(Entrada_A[4]), .Seletor(Seletor), .S(Entrada_A[5]),
    .Cout(celula_27_cout));
  Celula celula_28 (
    .Cin(celula_30_cout), .b(Entrada_B[4]), .a(Entrada_A[5]), .Seletor(Seletor), .S(Entrada_A[6]),
    .Cout(celula_28_cout));
  Celula celula_29 (
    .Cin(celula_27_cout), .b(Entrada_B[3]), .a(Entrada_A[2]), .Seletor(Seletor), .S(Entrada_A[3]),
    .Cout(celula_29_cout));
  Celula celula_30 (
    .Cin(celula_32_cout), .b(Entrada_B[2]), .a(Entrada_A[3]), .Seletor(Seletor), .S(Entrada_A[4]),
    .Cout(celula_30_cout));
  Celula celula_31 (
    .Cin(celula_29_cout), .b(Entrada_B[1]), .a(Entrada_A[0]), .Seletor(Seletor), .S(Entrada_A[1]),
    .Cout(celula_31_cout));
  Celula celula_32 (
    .Cin(1'b0), .b(Entrada_B[0]), .a(Entrada_A[1]), .Seletor(Seletor), .S(Entrada_A[2]), .Cout(celula_32_cout));
  OverFlowControler overflowcontroler_1 (
    .Overflow(overflowcontroler_1_overflow), .Cin(celula_31_cout), .Seletor(Seletor), .a(Entrada_A[0]),
    .b(Entrada_B[1]), .s(\Saída_S [0]));
  // also tied to GND on the sheet: celula_2_s

  // Notes on the sheet:
  //   00000=AND
  //   00001=OR
  //   00010=XOR
  //   00011=NAND
  //   00100=SOMA INT
  //   00101=SOMA NAT
  //   00110=SUBTRAIR
  //   00111=DESLOCAMENTO ESQUERDA
  //   01000=DESLOCAMENTO DIREITA
  //   1
  //   Overflow
endmodule

module Celula (
  input  Cin,
  input  b,
  input  a,
  input  [4:0] Seletor,
  output S,
  output Cout
);

  wire and_1_out, and_2_out, nand_1_out, or_1_out, Somador_s, Somador_vai1, Subtrator_s, Subtrator_vai1,
       xor_1_out;

  and and_1 (and_1_out, a, b);
  or or_1 (or_1_out, a, b);
  xor xor_1 (xor_1_out, a, b);
  nand nand_1 (nand_1_out, a, b);
  Somador Somador (.a(a), .b(b), .Vem1(Cin), .Vai1(Somador_vai1), .S(Somador_s));
  Subtrator Subtrator (.a(a), .b(b), .Vem1(Cin), .Vai1(Subtrator_vai1), .S(Subtrator_s));
  Multiplexer #(.enable("false")) multiplexer_1 (.in0(Somador_vai1), .in1(Subtrator_vai1), .out(Cout), .sel(and_2_out));
  and and_2 (and_2_out, ~Seletor[0], Seletor[1], Seletor[2], ~Seletor[3], ~Seletor[4]);  // AND_Gate
  Multiplexer #(.select(5), .enable("false")) multiplexer_2 (
    .in0(and_1_out), .in1(or_1_out), .in2(xor_1_out), .in3(nand_1_out), .in4(Somador_s), .in5(Somador_s),
    .in6(Subtrator_s), .in7(a), .in8(a), .out(S), .sel(Seletor));  // open: in9, in10, in11, in12, in13, in14, in15, in16, in17, in18, in19, in20, in21, in22, in23, in24, in25, in26, in27, in28, in29, in30, in31

  // Notes on the sheet:
  //   00000=AND
  //   00001=OR
  //   00010=XOR
  //   00011=NAND
  //   00100=SOMA INT
  //   00101=SOMA NAT
  //   00110=SUBTRATOR
  //   00111=DESLOCAMENTO ESQUERDA
  //   01000=DESLOCAMENTO DIREITA
endmodule

module OverFlowControler (
  input  Cin,
  input  a,
  input  b,
  input  s,
  input  [4:0] Seletor,
  output Overflow
);

  wire and_1_out, and_2_out, and_3_out, or_1_out;

  Multiplexer #(.enable("false")) multiplexer_1 (.in0(Cin), .in1(or_1_out), .out(Overflow), .sel(and_1_out));
  and and_1 (and_1_out, Seletor[0], ~Seletor[1], Seletor[2], ~Seletor[3], ~Seletor[4]);  // AND_Gate
  or or_1 (or_1_out, and_2_out, and_3_out);
  and and_2 (and_2_out, a, b, ~s);  // AND_Gate
  and and_3 (and_3_out, ~a, ~b, s);  // AND_Gate

  // Notes on the sheet:
  //   00100 - Soma de Naturais
  //   00101 - Soma de Inteiros
endmodule

module Somador (
  input  Vem1,
  input  a,
  input  b,
  output S,
  output Vai1
);

  wire and_1_out, and_2_out, and_3_out, xor_1_out;

  and and_1 (and_1_out, b, a);
  and and_2 (and_2_out, b, Vem1);
  or or_1 (Vai1, and_1_out, and_2_out, and_3_out);
  and and_3 (and_3_out, a, Vem1);
  xor xor_1 (xor_1_out, a, b);
  xor xor_2 (S, Vem1, xor_1_out);
endmodule

module Subtrator (
  input  Vem1,
  input  a,
  input  b,
  output S,
  output Vai1
);

  wire and_1_out, and_2_out, and_3_out, xor_1_out;

  and and_1 (and_1_out, b, ~a);  // AND_Gate
  and and_2 (and_2_out, b, Vem1);
  or or_1 (Vai1, and_1_out, and_2_out, and_3_out);
  and and_3 (and_3_out, ~a, Vem1);  // AND_Gate
  xor xor_1 (xor_1_out, a, b);
  xor xor_2 (S, Vem1, xor_1_out);
endmodule
